# Fritzing sketch 221005 irremote (saved by Fritzing 0.9.10b)
breadboards: 1

parts:
  Arduino2 = Arduino Uno (Rev3)
  블루투스 = Bluetooth HC-06u [package=THT]
  적외선센서 = KY-022 Infrared Receiver Module [package="Breakout board"]

nets:
  GND: Arduino2.GND, 블루투스.GND, 적외선센서.-
  N1: Arduino2.D2, 적외선센서.S
  N2: Arduino2.D3_PWM, 블루투스.RXD
  N3: Arduino2.D4, 블루투스.TXD
  5V: Arduino2.5V, 블루투스.VCC, 적외선센서.Vin

custom parts:
  Bluetooth HC-06u: Bluetooth HC-06 - face up, pins down 16.5mm x 37.5mm PCB
  KY-022 Infrared Receiver Module: KY-022 IR receiver module, reacts to 38kHz infrared light.
