# Fritzing sketch 221007 irSender (saved by Fritzing 0.9.10b)
breadboards: 3

parts:
  Arduino2 = Arduino Uno (Rev3)
  Mod1 = KY-005 Infrared Transmitter Module [package="Breakout board"]
  S1 = Pushbutton [package="[THT]"]
  R1 = Resistor [tolerance=±5% power=0.25 resistance=10k package=THT]
  R2 = Resistor [tolerance=±5% power=0.25 resistance=6.2k package=THT]
  S2 = Pushbutton [package="[THT]"]
  R3 = Resistor [tolerance=±5% power=0.25 resistance=4.7k package=THT]
  S3 = Pushbutton [package="[THT]"]
  S4 = Pushbutton [package="[THT]"]
  R4 = Resistor [tolerance=±5% power=0.25 resistance=10k package=THT]
  S5 = Pushbutton [package="[THT]"]
  R5 = Resistor [tolerance=±5% power=0.25 resistance=6.2k package=THT]
  S6 = Pushbutton [package="[THT]"]
  R6 = Resistor [tolerance=±5% power=0.25 resistance=4.7k package=THT]
  R7 = Resistor [tolerance=±5% power=0.25 resistance=3.3k package=THT]
  R8 = Resistor [tolerance=±5% power=0.25 resistance=3.3k package=THT]
  D7 = Rectifier Diode [part_number=1N4001 package="300 mil [THT]"]
  D8 = Rectifier Diode [part_number=1N4001 package="300 mil [THT]"]
  D10 = Rectifier Diode [part_number=1N4001 package="300 mil [THT]"]
  D11 = Rectifier Diode [part_number=1N4001 package="300 mil [THT]"]
  D12 = Rectifier Diode [part_number=1N4001 package="300 mil [THT]"]
  D9 = Rectifier Diode [part_number=1N4001 package="300 mil [THT]"]

nets:
  N1: Arduino2.A0, R7.Pin_1, D7.cathode, D8.cathode, D9.cathode
  N2: Arduino2.A1, R8.Pin_1, D10.cathode, D11.cathode, D12.cathode
  N3: Arduino2.D2, Mod1.S
  N4: Arduino2.D3_PWM, R4.Pin_0, R5.Pin_0, R6.Pin_0
  N5: Arduino2.D4, R1.Pin_0, R2.Pin_0, R3.Pin_0
  5V: Arduino2.5V, Mod1.Vin
  N6: Arduino2.GND, Mod1.-, R7.Pin_0, R8.Pin_0
  N7: S1.Pin_1, S1.Pin_2, D7.anode
  N8: S1.Pin_3, S1.Pin_4, R1.Pin_1
  N9: R2.Pin_1, S2.Pin_3, S2.Pin_4
  N10: S2.Pin_1, S2.Pin_2, D8.anode
  N11: R3.Pin_1, S3.Pin_3, S3.Pin_4
  N12: S3.Pin_1, S3.Pin_2, D9.anode
  N13: S4.Pin_1, S4.Pin_2, D10.anode
  N14: S4.Pin_3, S4.Pin_4, R4.Pin_1
  N15: S5.Pin_1, S5.Pin_2, D11.anode
  N16: S5.Pin_3, S5.Pin_4, R5.Pin_1
  N17: S6.Pin_1, S6.Pin_2, D12.anode
  N18: S6.Pin_3, S6.Pin_4, R6.Pin_1

custom parts:
  KY-005 Infrared Transmitter Module: Arduino IR Transmitter Module Keyes KY-005, emits infrared light at 38KHz.
