# Fritzing sketch 221013 Rasp3 ky-022 (saved by Fritzing 0.9.10b)

parts:
  Mod1 = KY-022 Infrared Receiver Module [package="Breakout board"]
  Raspberry_Pi1 = Raspberry Pi B+

nets:
  N1: Mod1.-, Raspberry_Pi1.GND
  VIN: Mod1.Vin, Raspberry_Pi1.5V
  N2: Mod1.S, Raspberry_Pi1.GPIO18

custom parts:
  KY-022 Infrared Receiver Module: KY-022 IR receiver module, reacts to 38kHz infrared light.
