# Fritzing sketch 221014 irSender (saved by Fritzing 0.9.10b)
breadboards: 6

parts:
  Mod1 = KY-005 Infrared Transmitter Module [package="Breakout board"]
  S1 = Pushbutton [package="[THT]"]
  D7 = Rectifier Diode [part_number=1N4001 package="300 mil [THT]"]
  부품1 = Arduino Nano (Rev3.0)
  R10 = Resistor [tolerance=±5% power=0.25 resistance=10k package=THT]
  S7 = Pushbutton [package="[THT]"]
  S8 = Pushbutton [package="[THT]"]
  D14 = Rectifier Diode [part_number=1N4001 package="300 mil [THT]"]
  R12 = Resistor [tolerance=±5% power=0.25 resistance=6.2k package=THT]
  R13 = Resistor [tolerance=±5% power=0.25 resistance=4.7k package=THT]
  D15 = Rectifier Diode [part_number=1N4001 package="300 mil [THT]"]
  S9 = Pushbutton [package="[THT]"]
  S10 = Pushbutton [package="[THT]"]
  S11 = Pushbutton [package="[THT]"]
  D16 = Rectifier Diode [part_number=1N4001 package="300 mil [THT]"]
  D17 = Rectifier Diode [part_number=1N4001 package="300 mil [THT]"]
  D18 = Rectifier Diode [part_number=1N4001 package="300 mil [THT]"]
  S12 = Pushbutton [package="[THT]"]
  S13 = Pushbutton [package="[THT]"]
  S14 = Pushbutton [package="[THT]"]
  D19 = Rectifier Diode [part_number=1N4001 package="300 mil [THT]"]
  D20 = Rectifier Diode [part_number=1N4001 package="300 mil [THT]"]
  D21 = Rectifier Diode [part_number=1N4001 package="300 mil [THT]"]
  S15 = Pushbutton [package="[THT]"]
  S16 = Pushbutton [package="[THT]"]
  S17 = Pushbutton [package="[THT]"]
  D22 = Rectifier Diode [part_number=1N4001 package="300 mil [THT]"]
  D23 = Rectifier Diode [part_number=1N4001 package="300 mil [THT]"]
  D24 = Rectifier Diode [part_number=1N4001 package="300 mil [THT]"]
  R14 = Resistor [tolerance=±5% power=0.25 resistance=3.3k package=THT]
  S18 = Pushbutton [package="[THT]"]
  S19 = Pushbutton [package="[THT]"]
  S20 = Pushbutton [package="[THT]"]
  S21 = Pushbutton [package="[THT]"]
  S22 = Pushbutton [package="[THT]"]
  S23 = Pushbutton [package="[THT]"]
  S24 = Pushbutton [package="[THT]"]
  S25 = Pushbutton [package="[THT]"]
  S26 = Pushbutton [package="[THT]"]
  S27 = Pushbutton [package="[THT]"]
  S28 = Pushbutton [package="[THT]"]
  S29 = Pushbutton [package="[THT]"]
  D25 = Rectifier Diode [part_number=1N4001 package="300 mil [THT]"]
  D26 = Rectifier Diode [part_number=1N4001 package="300 mil [THT]"]
  D27 = Rectifier Diode [part_number=1N4001 package="300 mil [THT]"]
  D28 = Rectifier Diode [part_number=1N4001 package="300 mil [THT]"]
  D29 = Rectifier Diode [part_number=1N4001 package="300 mil [THT]"]
  D30 = Rectifier Diode [part_number=1N4001 package="300 mil [THT]"]
  D31 = Rectifier Diode [part_number=1N4001 package="300 mil [THT]"]
  D32 = Rectifier Diode [part_number=1N4001 package="300 mil [THT]"]
  D33 = Rectifier Diode [part_number=1N4001 package="300 mil [THT]"]
  D34 = Rectifier Diode [part_number=1N4001 package="300 mil [THT]"]
  D35 = Rectifier Diode [part_number=1N4001 package="300 mil [THT]"]
  D36 = Rectifier Diode [part_number=1N4001 package="300 mil [THT]"]
  R15 = Resistor [tolerance=±5% power=0.25 resistance=3.3k package=THT]
  R16 = Resistor [tolerance=±5% power=0.25 resistance=4.7k package=THT]
  R17 = Resistor [tolerance=±5% power=0.25 resistance=6.2k package=THT]
  R18 = Resistor [tolerance=±5% power=0.25 resistance=10k package=THT]

nets:
  N1: Mod1.S, 부품1.D2
  VIN: Mod1.Vin, 부품1.5V
  N2: Mod1.-, 부품1.GND, R14.Pin_0, R15.Pin_0
  N3: S1.Pin_1, S1.Pin_2, R10.Pin_0, S9.Pin_1, S9.Pin_2, S12.Pin_1, S12.Pin_2, S15.Pin_1, S15.Pin_2
  N4: S1.Pin_3, S1.Pin_4, D7.cathode
  N5: D7.anode, 부품1.D10, D14.anode, D15.anode, D25.anode, D31.anode, D33.anode
  N6: 부품1.D7, D22.anode, D23.anode, D24.anode, D26.anode, D30.anode, D32.anode
  N7: 부품1.D8, D19.anode, D20.anode, D21.anode, D29.anode, D34.anode, D36.anode
  N8: 부품1.D9, D16.anode, D17.anode, D18.anode, D27.anode, D28.anode, D35.anode
  N9: 부품1.A1, R10.Pin_1, R12.Pin_1, R13.Pin_1, R14.Pin_1
  N10: 부품1.A0, R15.Pin_1, R16.Pin_1, R17.Pin_1, R18.Pin_1
  N11: S7.Pin_1, S7.Pin_2, R12.Pin_0, S11.Pin_1, S11.Pin_2, S14.Pin_1, S14.Pin_2, S17.Pin_1, S17.Pin_2
  N12: S7.Pin_3, S7.Pin_4, D15.cathode
  N13: S8.Pin_1, S8.Pin_2, R13.Pin_0, S10.Pin_1, S10.Pin_2, S13.Pin_1, S13.Pin_2, S16.Pin_1, S16.Pin_2
  N14: S8.Pin_3, S8.Pin_4, D14.cathode
  N15: S9.Pin_3, S9.Pin_4, D16.cathode
  N16: S10.Pin_3, S10.Pin_4, D18.cathode
  N17: S11.Pin_3, S11.Pin_4, D17.cathode
  N18: S12.Pin_3, S12.Pin_4, D19.cathode
  N19: S13.Pin_3, S13.Pin_4, D21.cathode
  N20: S14.Pin_3, S14.Pin_4, D20.cathode
  N21: S15.Pin_3, S15.Pin_4, D22.cathode
  N22: S16.Pin_3, S16.Pin_4, D24.cathode
  N23: S17.Pin_3, S17.Pin_4, D23.cathode
  N24: S18.Pin_1, S18.Pin_2, S23.Pin_1, S23.Pin_2, S28.Pin_1, S28.Pin_2, S29.Pin_1, S29.Pin_2, R18.Pin_0
  N25: S18.Pin_3, S18.Pin_4, D25.cathode
  N26: S19.Pin_1, S19.Pin_2, S21.Pin_1, S21.Pin_2, S25.Pin_1, S25.Pin_2, S26.Pin_1, S26.Pin_2, R16.Pin_0
  N27: S19.Pin_3, S19.Pin_4, D34.cathode
  N28: S20.Pin_1, S20.Pin_2, S22.Pin_1, S22.Pin_2, S24.Pin_1, S24.Pin_2, S27.Pin_1, S27.Pin_2, R17.Pin_0
  N29: S20.Pin_3, S20.Pin_4, D33.cathode
  N30: S21.Pin_3, S21.Pin_4, D32.cathode
  N31: S22.Pin_3, S22.Pin_4, D27.cathode
  N32: S23.Pin_3, S23.Pin_4, D36.cathode
  N33: S24.Pin_3, S24.Pin_4, D30.cathode
  N34: S25.Pin_3, S25.Pin_4, D35.cathode
  N35: S26.Pin_3, S26.Pin_4, D31.cathode
  N36: S27.Pin_3, S27.Pin_4, D29.cathode
  N37: S28.Pin_3, S28.Pin_4, D28.cathode
  N38: S29.Pin_3, S29.Pin_4, D26.cathode

custom parts:
  KY-005 Infrared Transmitter Module: Arduino IR Transmitter Module Keyes KY-005, emits infrared light at 38KHz.
