# Fritzing sketch 221102 HallSensor(WSH138) (saved by Fritzing 0.9.10b)
breadboards: 1

parts:
  부품1 = Arduino Nano (Rev3.0)
  WSH138 = Hall Sensor [part_number=WSH130 package=TO92]

nets:
  GND: 부품1.GND, WSH138.GND
  5V: 부품1.5V, WSH138.VCC
  N1: 부품1.A0, WSH138.OUT

custom parts:
  Hall Sensor: A Hall Sensor
